// Logisim project P2_Mux8.circ as structural Verilog: 1 circuit, main circuit P2_Mux8
module P2_Mux8 (
  input  [7:0] din,
  input  [2:0] sel,
  output data
);

  Multiplexer #(.select(3), .width(1), .enable("false")) multiplexer_1 (
    .in0(din[0]), .in1(din[1]), .in2(din[2]), .in3(din[3]), .in4(din[4]), .in5(din[5]), .in6(din[6]),
    .in7(din[7]), .out(data), .sel(sel));

  // Notes on the sheet:
  //   din: initial=0xa5
  //   2. 8-to-1 multiplexer
  //   INPUTS: din[7:0], sel[2:0]                            OUTPUT: data (1 bit)
  //   sel=000 selects din[0]; sel=111 selects din[7]. All 2,048 input combinations tested.
  //   din[0]
  //   din[1]
  //   din[2]
  //   din[3]
  //   din[4]
  //   din[5]
  //   din[6]
  //   din[7]
endmodule
